# Fritzing sketch SAE-2021-TestRig (saved by Fritzing 0.9.8b)
breadboards: 2

parts:
  Front_CAN = Waveshare SN65HVD230 CAN Board [chip_label=SN65HVD230]
  Back_CAN = Waveshare SN65HVD230 CAN Board [chip_label=Yes]
  R15 = Resistor [tolerance=±5% resistance=1k power=0.25 package=THT]
  R16 = Resistor [tolerance=±5% resistance=1k power=0.25 package=THT]
  R17 = Resistor [tolerance=±5% resistance=1k power=0.25 package=THT]
  R19 = Resistor [tolerance=±5% resistance=1k power=0.25 package=THT]
  R20 = Resistor [tolerance=±5% resistance=1k power=0.25 package=THT]
  R21 = Resistor [tolerance=±5% resistance=220 power=0.25 package=THT]
  R22 = Resistor [tolerance=±5% resistance=220 power=0.25 package=THT]
  R23 = Resistor [tolerance=±5% resistance=220 power=0.25 package=THT]
  R24 = Resistor [tolerance=±5% resistance=220 power=0.25 package=THT]
  R25 = Resistor [tolerance=±5% resistance=220 power=0.25 package=THT]
  R26 = Resistor [tolerance=±5% resistance=220 power=0.25 package=THT]
  R27 = Resistor [tolerance=±5% resistance=220 power=0.25 package=THT]
  R28 = Resistor [tolerance=±5% resistance=220 power=0.25 package=THT]
  R29 = Resistor [tolerance=±5% resistance=220 power=0.25 package=THT]
  R30 = Resistor [tolerance=±5% resistance=220 power=0.25 package=THT]
  FAN_2 = LED - 3mm [color="White (6500K)" current=0.030 package="3 mm [THT]"]
  R31 = Resistor [tolerance=±5% resistance=220 power=0.25 package=THT]
  Servos_Off = LED - 3mm [color="Yellow (595nm)" current=0.030 package="3 mm [THT]"]
  FAN_4 = LED - 3mm [color="White (6500K)" current=0.030 package="3 mm [THT]"]
  R32 = Resistor [tolerance=±5% resistance=220 power=0.25 package=THT]
  Pedal = Rotary Potentiometer (Small) [maximum_resistance=5kΩ package=THT]
  Steering = Rotary Potentiometer (Small) [maximum_resistance=5kΩ package=THT]
  Start_button = Momentary Switch [package=ksa_sealed_tac_switch]
  Start = LED - 3mm [color="Green (555nm)" current=0.030 package="3 mm [THT]"]
  IMD = LED - 3mm [color="Red (633nm)" current=0.030 package="3 mm [THT]"]
  BMS = LED - 3mm [color="Red (633nm)" current=0.030 package="3 mm [THT]"]
  R33 = Resistor [tolerance=±5% resistance=220 power=0.25 package=THT]
  R34 = Resistor [tolerance=±5% resistance=220 power=0.25 package=THT]
  R35 = Resistor [tolerance=±5% resistance=220 power=0.25 package=THT]
  Air_2 = LED - 3mm [color="Yellow (595nm)" current=0.030 package="3 mm [THT]"]
  Charge_Relay = LED - 3mm [color="Yellow (595nm)" current=0.030 package="3 mm [THT]"]
  Run_Speaker = LED - 3mm [color="Yellow (595nm)" current=0.030 package="3 mm [THT]"]
  Aero_Servo_1 = LED - 3mm [color="Yellow (595nm)" current=0.030 package="3 mm [THT]"]
  Brake_Light = LED - 3mm [color="Yellow (595nm)" current=0.030 package="3 mm [THT]"]
  Fans_on = LED - 3mm [color="Yellow (595nm)" current=0.030 package="3 mm [THT]"]
  PreCharge_Relay = LED - 3mm [color="Yellow (595nm)" current=0.030 package="3 mm [THT]"]
  Air_1 = LED - 3mm [color="Yellow (595nm)" current=0.030 package="3 mm [THT]"]
  Aero_Servo_2 = LED - 3mm [color="Yellow (595nm)" current=0.030 package="3 mm [THT]"]
  Pump_DAC = LED - 3mm [color="Yellow (595nm)" current=0.030 package="3 mm [THT]"]
  Dip_Switch = DIP Switch 8 Position [package=dipswitch-08]
  Brake = Rotary Potentiometer (Small) [maximum_resistance=5kΩ package=THT]
  Back_Teensy = Teensy 3.6 (Basic)
  Front_Teensy = Teensy 3.6 (Basic)

nets:
  3.3V: Front_CAN.3.3v, Back_CAN.3.3v, Pedal.leg1, Steering.leg1, Start_button.2, Brake.leg1, Front_Teensy.3V3, Front_Teensy.3V3_1
  GND: Front_CAN.GND, Back_CAN.GND, R32.Pin_1, Pedal.leg2, Steering.leg2, R33.Pin_1, R34.Pin_1, R35.Pin_1, Brake.leg2, Front_Teensy.GND
  N1: Front_CAN.CAN_RX, Front_Teensy.D34
  N2: Front_CAN.CAN_TX, Front_Teensy.D33
  N3: Front_CAN.CAN_L, Back_CAN.CAN_L
  N4: Front_CAN.CAN_H, Back_CAN.CAN_H
  N5: Back_CAN.CAN_RX, Back_Teensy.D34
  N6: Back_CAN.CAN_TX, Back_Teensy.D33
  N7: R15.Pin_0, Dip_Switch.3, Back_Teensy.D26
  N8: R15.Pin_1, R16.Pin_1, R17.Pin_1, R19.Pin_1, R20.Pin_1, R21.Pin_0, R22.Pin_0, R23.Pin_0, R24.Pin_0, R25.Pin_0, R26.Pin_0, R27.Pin_0, R28.Pin_0, R29.Pin_0, R30.Pin_0, FAN_2.cathode, R31.Pin_0, FAN_4.cathode, Back_Teensy.GND
  N9: R16.Pin_0, Dip_Switch.4, Back_Teensy.A5/D19
  N10: R17.Pin_0, Dip_Switch.5, Back_Teensy.A4/D18
  N11: R19.Pin_0, Dip_Switch.1, Back_Teensy.D3
  N12: R20.Pin_0, Dip_Switch.2, Back_Teensy.D25
  N13: R21.Pin_1, Servos_Off.cathode
  N14: R22.Pin_1, Air_2.cathode
  N15: R23.Pin_1, Charge_Relay.cathode
  N16: R24.Pin_1, Run_Speaker.cathode
  N17: R25.Pin_1, Brake_Light.cathode
  N18: R26.Pin_1, Aero_Servo_1.cathode
  N19: R27.Pin_1, PreCharge_Relay.cathode
  N20: R28.Pin_1, Air_1.cathode
  N21: R29.Pin_1, Fans_on.cathode
  N22: R30.Pin_1, Aero_Servo_2.cathode
  N23: FAN_2.anode, Back_Teensy.A8/D22, Back_Teensy.A10
  N24: R31.Pin_1, Pump_DAC.cathode
  N25: Servos_Off.anode, Back_Teensy.D0
  N26: FAN_4.anode, Back_Teensy.A6/D20
  N27: R32.Pin_0, Start_button.4, Front_Teensy.D2
  N28: Pedal.wiper, Front_Teensy.A2/D16, Front_Teensy.A4/D18
  N29: Steering.wiper, Front_Teensy.A1/D15
  N30: Start.cathode, R35.Pin_0
  N31: Start.anode, Front_Teensy.D36
  N32: IMD.cathode, R33.Pin_0
  N33: IMD.anode, Front_Teensy.D38, Front_Teensy.R
  N34: BMS.cathode, R34.Pin_0
  N35: BMS.anode, Front_Teensy.D37
  N36: Air_2.anode, Back_Teensy.D4
  N37: Charge_Relay.anode, Back_Teensy.D5
  N38: Run_Speaker.anode, Back_Teensy.D6
  N39: Aero_Servo_1.anode, Back_Teensy.D8
  N40: Brake_Light.anode, Back_Teensy.D7
  N41: Fans_on.anode, Back_Teensy.D24
  N42: PreCharge_Relay.anode, Back_Teensy.D9
  N43: Air_1.anode, Back_Teensy.D10
  N44: Aero_Servo_2.anode, Back_Teensy.D30
  N45: Pump_DAC.anode, Back_Teensy.A21/DAC0
  N46: Dip_Switch.12, Dip_Switch.13, Dip_Switch.14, Dip_Switch.15, Dip_Switch.16, Back_Teensy.3V3, Back_Teensy.3V3_1
  N47: Brake.wiper, Front_Teensy.A0/D14
  N48: Back_Teensy.A7/D21, Back_Teensy.A11
  N49: Back_Teensy.A9/D23, Back_Teensy.AREF
  N50: Back_Teensy.AGND, Back_Teensy.VUSB
  N51: Back_Teensy.D27, Back_Teensy.3V, Back_Teensy.Vb
  N52: Back_Teensy.D38, Back_Teensy.R
  N53: Front_Teensy.A7/D21, Front_Teensy.A11
  N54: Front_Teensy.A8/D22, Front_Teensy.A10
  N55: Front_Teensy.A9/D23, Front_Teensy.AREF
  N56: Front_Teensy.AGND, Front_Teensy.VUSB
  N57: Front_Teensy.D27, Front_Teensy.3V, Front_Teensy.Vb

notes:
  TSV
  Shutdown
  HVD Fault
  IMD Fault
  BMS Fault

custom parts:
  Waveshare SN65HVD230 CAN Board: Waveshare SN65HVD230 CAN Board Connecting MCUs to CAN Network Features ESD Protection Communication Evaluation Development Board 3.3V
  Teensy 3.6 (Basic): The Teensy is a complete USB-based microcontoller development system, in a very small footprint, capable of implementing many types of projects. All programming is done via the USB port. No special programmer is needed, only a standard micro-USB cable and a PC or Macintosh with a USB port.
